// Logisim project 8BitBenEater.circ as structural Verilog: 9 circuits, main circuit main
module main (
  input  in_1,
  input  in_2,
  input  in_3,
  input  PROGRAM_MODE
);

  wire bcd_to_7_segment_decoder_2_p1, bcd_to_7_segment_decoder_3_p1, binary_to_bcd_converter_1_p2,
       button_1_out, clock_1_out, mar_1_p1, mar_1_p5, multiplexer_2_out, not_1_out;
  wire [3:0] dipswitch_2_sw4, mar_1_p2, mar_1_p3, multiplexer_3_out;
  wire [7:0] binary_to_bcd_converter_1_p1, dipswitch_1_sw8, memory_1_always_out, multiplexer_1_out,
       register_a_1_always_out, register_b_1_always_out;
  wire [7:4] memory_1_ram_out;

  DipSwitch dipswitch_1 (
    .sw1(dipswitch_1_sw8[7]), .sw2(dipswitch_1_sw8[6]), .sw3(dipswitch_1_sw8[5]), .sw4(dipswitch_1_sw8[4]),
    .sw5(dipswitch_1_sw8[3]), .sw6(dipswitch_1_sw8[2]), .sw7(dipswitch_1_sw8[1]), .sw8(dipswitch_1_sw8[0]));
  Button button_1 (.out(button_1_out));
  LED led_1 (.in(not_1_out));
  not not_1 (not_1_out, PROGRAM_MODE);
  DipSwitch #(.number(4)) dipswitch_2 (
    .sw1(dipswitch_2_sw4[3]), .sw2(dipswitch_2_sw4[2]), .sw3(dipswitch_2_sw4[1]), .sw4(dipswitch_2_sw4[0]));
  LED led_2 (.in(PROGRAM_MODE));
  Multiplexer #(.width(8)) multiplexer_1 (
    .in0({memory_1_ram_out, mar_1_p3}), .in1(dipswitch_1_sw8), .out(multiplexer_1_out), .sel(PROGRAM_MODE));
  Multiplexer multiplexer_2 (.in1(button_1_out), .out(multiplexer_2_out), .sel(PROGRAM_MODE));  // open: in0
  Clock clock_1 (.out(clock_1_out));
  Multiplexer #(.width(4)) multiplexer_3 (
    .in0(mar_1_p2), .in1(dipswitch_2_sw4), .out(multiplexer_3_out), .sel(PROGRAM_MODE));
  // MAR mar_1: pin names not known; wires that end beside it: mar_1_p1, mar_1_p2, mar_1_p3, mar_1_p3, mar_1_p5, mar_1_p5
  LED led_3 (.in(multiplexer_3_out[3]));
  LED led_4 (.in(multiplexer_3_out[2]));
  LED led_5 (.in(multiplexer_3_out[1]));
  LED led_6 (.in(memory_1_always_out[7]));
  LED led_7 (.in(memory_1_always_out[6]));
  LED led_8 (.in(memory_1_always_out[5]));
  LED led_9 (.in(multiplexer_3_out[0]));
  MEMORY memory_1 (
    .STORE(multiplexer_2_out), .CLOCK(mar_1_p1), .ADDRESS(multiplexer_3_out), .DATA(multiplexer_1_out),
    .ALWAYS_OUT(memory_1_always_out), .RAM_OUT({memory_1_ram_out, mar_1_p3}));  // open: RAM_OUT_ENB
  LED led_10 (.in(memory_1_always_out[4]));
  LED led_11 (.in(memory_1_always_out[3]));
  LED led_12 (.in(memory_1_always_out[2]));
  LED led_13 (.in(memory_1_always_out[1]));
  CLK clk_1 (.CLK_IN(clock_1_out), .CLK_ENB(in_1), .CLK_MANUAL(in_2), .HALT(in_3), .CLK_OUT(mar_1_p1));
  LED led_14 (.in(memory_1_always_out[0]));
  LED led_15 (.in(memory_1_ram_out[7]));
  LED led_16 (.in(memory_1_ram_out[6]));
  LED led_17 (.in(memory_1_ram_out[5]));
  LED led_18 (.in(memory_1_ram_out[4]));
  Pull_Resistor pull_resistor_1 (.node(memory_1_ram_out[7]));
  Pull_Resistor pull_resistor_2 (.node(memory_1_ram_out[6]));
  Pull_Resistor pull_resistor_3 (.node(memory_1_ram_out[5]));
  Pull_Resistor pull_resistor_4 (.node(memory_1_ram_out[4]));
  LED led_19 (.in(mar_1_p3[3]));
  LED led_20 (.in(mar_1_p3[2]));
  LED led_21 (.in(mar_1_p3[1]));
  LED led_22 (.in(mar_1_p3[0]));
  Pull_Resistor pull_resistor_5 (.node(mar_1_p3[3]));
  Pull_Resistor pull_resistor_6 (.node(mar_1_p3[2]));
  Pull_Resistor pull_resistor_7 (.node(mar_1_p3[1]));
  Pull_Resistor pull_resistor_8 (.node(mar_1_p3[0]));
  PROGRAM_COUNTER program_counter_1 (
    .CLOCK(mar_1_p1), .ADDRESS_IN(mar_1_p3), .ADDRESS_OUT(mar_1_p3));  // open: RESET, JUMP, COUNTER_ENABLE, COUNTER_OUT, ALWAYS_OUT
  REGISTER_A register_a_1 (
    .DATA_IN({memory_1_ram_out, mar_1_p3}), .CLOCK(mar_1_p1), .ALWAYS_OUT(register_a_1_always_out),
    .DATA_OUT({memory_1_ram_out, mar_1_p3}));  // open: A_IN, A_OUT, A_RESET
  REGISTER_B register_b_1 (
    .CLOCK(mar_1_p1), .DATA_IN({memory_1_ram_out, mar_1_p3}), .ALWAYS_OUT(register_b_1_always_out));  // open: B_IN, B_OUT, RESET, DATA_OUT
  _7_Segment_Display u_7_segment_display_1 ();  // open: g, f, a, b, e, d, c, dp
  _7_Segment_Display u_7_segment_display_2 ();  // open: g, f, a, b, e, d, c, dp
  // BCD_to_7_Segment_decoder bcd_to_7_segment_decoder_1: pin names not known
  // BCD_to_7_Segment_decoder bcd_to_7_segment_decoder_2: pin names not known; wires that end beside it: bcd_to_7_segment_decoder_2_p1
  // Binary_to_BCD_converter #(.binvalue(8)) binary_to_bcd_converter_1: pin names not known; wires that end beside it: binary_to_bcd_converter_1_p1, binary_to_bcd_converter_1_p2, binary_to_bcd_converter_1_p2, bcd_to_7_segment_decoder_2_p1
  OUTPUT_REGISTER output_register_1 (
    .CLOCK(mar_1_p1), .DATA_IN({memory_1_ram_out, mar_1_p3}), .DATA_OUT(binary_to_bcd_converter_1_p1));  // open: STORE, RESET
  ALU alu_1 (
    .A_IN(register_a_1_always_out), .B_IN(register_b_1_always_out),
    .ALU_DATA_OUT({memory_1_ram_out, mar_1_p3}));  // open: OUTPUT_ENB, SUB, ALWAYS_OUT, COUT
  _7_Segment_Display u_7_segment_display_3 ();  // open: g, f, a, b, e, d, c, dp
  // BCD_to_7_Segment_decoder bcd_to_7_segment_decoder_3: pin names not known; wires that end beside it: bcd_to_7_segment_decoder_3_p1, bcd_to_7_segment_decoder_3_p1
endmodule

module CLK (
  input  CLK_IN,
  input  CLK_ENB,
  input  CLK_MANUAL,
  input  HALT,
  output CLK_OUT
);

  wire and_1_out, and_2_out, not_1_out, not_2_out, or_1_out;

  not not_1 (not_1_out, CLK_ENB);
  not not_2 (not_2_out, HALT);
  and and_1 (and_1_out, CLK_IN, CLK_ENB);
  and and_2 (and_2_out, not_1_out, CLK_MANUAL);
  or or_1 (or_1_out, and_1_out, and_2_out);
  and and_3 (CLK_OUT, or_1_out, not_2_out);
endmodule

module PROGRAM_COUNTER (
  input  RESET,
  input  JUMP,
  input  COUNTER_ENABLE,
  input  CLOCK,
  input  [3:0] ADDRESS_IN,
  input  COUNTER_OUT,
  output [3:0] ALWAYS_OUT,
  output [3:0] ADDRESS_OUT
);

  Counter #(.max('hf), .width(4)) counter_1 (
    .clr(RESET), .load(JUMP), .up(COUNTER_ENABLE), .count(COUNTER_ENABLE), .clk(CLOCK), .D(ADDRESS_IN),
    .Q(ALWAYS_OUT));  // open: carry
  assign ADDRESS_OUT = COUNTER_OUT ? ALWAYS_OUT : 4'bz;  // Controlled_Buffer controlled_buffer_1
endmodule

module REGISTER_A (
  input  [7:0] DATA_IN,
  input  A_IN,
  input  A_OUT,
  input  CLOCK,
  input  A_RESET,
  output [7:0] ALWAYS_OUT,
  output [7:0] DATA_OUT
);

  Register register_1 (.D(DATA_IN), .en(A_IN), .clk(CLOCK), .Q(ALWAYS_OUT), .clr(A_RESET));
  assign DATA_OUT = A_OUT ? ALWAYS_OUT : 8'bz;  // Controlled_Buffer controlled_buffer_1
endmodule

module ALU (
  input  [7:0] A_IN,
  input  [7:0] B_IN,
  input  OUTPUT_ENB,
  input  SUB,
  output [7:0] ALWAYS_OUT,
  output [7:0] ALU_DATA_OUT,
  output COUT
);

  wire not_1_out;
  wire [7:0] controlled_buffer_1_out, xor_1_out;

  assign controlled_buffer_1_out = SUB ? {8{1'b1}} : 8'bz;  // Controlled_Buffer controlled_buffer_1
  assign controlled_buffer_1_out = not_1_out ? {8{1'b0}} : 8'bz;  // Controlled_Buffer controlled_buffer_2
  not not_1 (not_1_out, SUB);
  assign xor_1_out = B_IN ^ controlled_buffer_1_out;  // XOR_Gate xor_1, 8 bits wide
  Adder adder_1 (.a(A_IN), .b(xor_1_out), .out(ALWAYS_OUT), .cin(SUB), .cout(COUT));
  assign ALU_DATA_OUT = OUTPUT_ENB ? ALWAYS_OUT : 8'bz;  // Controlled_Buffer controlled_buffer_3
endmodule

module REGISTER_B (
  input  [7:0] DATA_IN,
  input  B_IN,
  input  B_OUT,
  input  CLOCK,
  input  RESET,
  output [7:0] ALWAYS_OUT,
  output [7:0] DATA_OUT
);

  Register register_1 (.D(DATA_IN), .en(B_IN), .clk(CLOCK), .Q(ALWAYS_OUT), .clr(RESET));
  assign DATA_OUT = B_OUT ? ALWAYS_OUT : 8'bz;  // Controlled_Buffer controlled_buffer_1
endmodule

module OUTPUT_REGISTER (
  input  [7:0] DATA_IN,
  input  STORE,
  input  CLOCK,
  input  RESET,
  output [7:0] DATA_OUT
);

  Register register_1 (.D(DATA_IN), .en(STORE), .clk(CLOCK), .Q(DATA_OUT), .clr(RESET));
endmodule

module MAR (
  input  [3:0] DATA_IN,
  input  MAR_IN,
  input  MAR_OUT,
  input  CLOCK,
  input  MAR_RESET,
  output [3:0] ALWAYS_OUT,
  output [3:0] DATA_OUT
);

  Register #(.width(4)) register_1 (.D(DATA_IN), .en(MAR_IN), .clk(CLOCK), .Q(ALWAYS_OUT), .clr(MAR_RESET));
  assign DATA_OUT = MAR_OUT ? ALWAYS_OUT : 4'bz;  // Controlled_Buffer controlled_buffer_1
endmodule

module MEMORY (
  input  [7:0] DATA,
  input  STORE,
  input  CLOCK,
  input  [3:0] ADDRESS,
  input  RAM_OUT_ENB,
  output [7:0] ALWAYS_OUT,
  output [7:0] RAM_OUT
);

  wire and_1_out, and_2_out, and_3_out, and_4_out, and_5_out, and_6_out, and_7_out, and_8_out, and_9_out,
       and_10_out, and_11_out, and_12_out, and_13_out, and_14_out, and_15_out, and_16_out, decoder_1_out0,
       decoder_1_out1, decoder_1_out2, decoder_1_out3, decoder_1_out4, decoder_1_out5, decoder_1_out6,
       decoder_1_out7, decoder_1_out8, decoder_1_out9, decoder_1_out10, decoder_1_out11, decoder_1_out12,
       decoder_1_out13, decoder_1_out14, decoder_1_out15;
  wire [7:0] demultiplexer_1_out0, demultiplexer_1_out1, demultiplexer_1_out2, demultiplexer_1_out3,
       demultiplexer_1_out4, demultiplexer_1_out5, demultiplexer_1_out6, demultiplexer_1_out7,
       demultiplexer_1_out8, demultiplexer_1_out9, demultiplexer_1_out10, demultiplexer_1_out11,
       demultiplexer_1_out12, demultiplexer_1_out13, demultiplexer_1_out14, demultiplexer_1_out15,
       register_1_q, register_2_q, register_3_q, register_4_q, register_5_q, register_6_q, register_7_q,
       register_8_q, register_9_q, register_10_q, register_11_q, register_12_q, register_13_q, register_14_q,
       register_15_q, register_16_q;

  Demultiplexer #(.select(4), .width(8)) demultiplexer_1 (
    .out0(demultiplexer_1_out0), .out1(demultiplexer_1_out1), .out2(demultiplexer_1_out2),
    .out3(demultiplexer_1_out3), .out4(demultiplexer_1_out4), .out5(demultiplexer_1_out5),
    .out6(demultiplexer_1_out6), .out7(demultiplexer_1_out7), .out8(demultiplexer_1_out8),
    .out9(demultiplexer_1_out9), .out10(demultiplexer_1_out10), .out11(demultiplexer_1_out11),
    .out12(demultiplexer_1_out12), .out13(demultiplexer_1_out13), .out14(demultiplexer_1_out14),
    .out15(demultiplexer_1_out15), .in(DATA), .sel(ADDRESS));
  Decoder #(.select(4)) decoder_1 (
    .out0(decoder_1_out0), .out1(decoder_1_out1), .out2(decoder_1_out2), .out3(decoder_1_out3),
    .out4(decoder_1_out4), .out5(decoder_1_out5), .out6(decoder_1_out6), .out7(decoder_1_out7),
    .out8(decoder_1_out8), .out9(decoder_1_out9), .out10(decoder_1_out10), .out11(decoder_1_out11),
    .out12(decoder_1_out12), .out13(decoder_1_out13), .out14(decoder_1_out14), .out15(decoder_1_out15),
    .sel(ADDRESS));  // open: en
  and and_1 (and_1_out, decoder_1_out0, STORE);
  and and_2 (and_2_out, decoder_1_out1, STORE);
  and and_3 (and_3_out, decoder_1_out2, STORE);
  and and_4 (and_4_out, decoder_1_out3, STORE);
  and and_5 (and_5_out, decoder_1_out4, STORE);
  and and_6 (and_6_out, decoder_1_out5, STORE);
  and and_7 (and_7_out, decoder_1_out6, STORE);
  and and_8 (and_8_out, decoder_1_out7, STORE);
  and and_9 (and_9_out, decoder_1_out8, STORE);
  and and_10 (and_10_out, decoder_1_out9, STORE);
  and and_11 (and_11_out, decoder_1_out10, STORE);
  and and_12 (and_12_out, decoder_1_out11, STORE);
  and and_13 (and_13_out, decoder_1_out12, STORE);
  and and_14 (and_14_out, decoder_1_out13, STORE);
  and and_15 (and_15_out, decoder_1_out14, STORE);
  and and_16 (and_16_out, decoder_1_out15, STORE);
  Register register_1 (.D(demultiplexer_1_out0), .en(and_1_out), .clk(CLOCK), .Q(register_1_q));  // open: clr
  Register register_2 (.D(demultiplexer_1_out1), .en(and_2_out), .clk(CLOCK), .Q(register_2_q));  // open: clr
  Register register_3 (.D(demultiplexer_1_out2), .en(and_3_out), .clk(CLOCK), .Q(register_3_q));  // open: clr
  Register register_4 (.D(demultiplexer_1_out3), .en(and_4_out), .clk(CLOCK), .Q(register_4_q));  // open: clr
  Register register_5 (.D(demultiplexer_1_out4), .en(and_5_out), .clk(CLOCK), .Q(register_5_q));  // open: clr
  Register register_6 (.D(demultiplexer_1_out5), .en(and_6_out), .clk(CLOCK), .Q(register_6_q));  // open: clr
  Register register_7 (.D(demultiplexer_1_out6), .en(and_7_out), .clk(CLOCK), .Q(register_7_q));  // open: clr
  Register register_8 (.D(demultiplexer_1_out7), .en(and_8_out), .clk(CLOCK), .Q(register_8_q));  // open: clr
  Register register_9 (.D(demultiplexer_1_out8), .en(and_9_out), .clk(CLOCK), .Q(register_9_q));  // open: clr
  Register register_10 (.D(demultiplexer_1_out9), .en(and_10_out), .clk(CLOCK), .Q(register_10_q));  // open: clr
  Register register_11 (.D(demultiplexer_1_out10), .en(and_11_out), .clk(CLOCK), .Q(register_11_q));  // open: clr
  Register register_12 (.D(demultiplexer_1_out11), .en(and_12_out), .clk(CLOCK), .Q(register_12_q));  // open: clr
  Register register_13 (.D(demultiplexer_1_out12), .en(and_13_out), .clk(CLOCK), .Q(register_13_q));  // open: clr
  Register register_14 (.D(demultiplexer_1_out13), .en(and_14_out), .clk(CLOCK), .Q(register_14_q));  // open: clr
  Register register_15 (.D(demultiplexer_1_out14), .en(and_15_out), .clk(CLOCK), .Q(register_15_q));  // open: clr
  Register register_16 (.D(demultiplexer_1_out15), .en(and_16_out), .clk(CLOCK), .Q(register_16_q));  // open: clr
  Multiplexer #(.select(4), .width(8)) multiplexer_1 (
    .in0(register_1_q), .in1(register_2_q), .in2(register_3_q), .in3(register_4_q), .in4(register_5_q),
    .in5(register_6_q), .in6(register_7_q), .in7(register_8_q), .in8(register_9_q), .in9(register_10_q),
    .in10(register_11_q), .in11(register_12_q), .in12(register_13_q), .in13(register_14_q),
    .in14(register_15_q), .in15(register_16_q), .out(ALWAYS_OUT), .sel(ADDRESS));
  assign RAM_OUT = RAM_OUT_ENB ? ALWAYS_OUT : 8'bz;  // Controlled_Buffer controlled_buffer_1
endmodule
